// Logisim project alu.circ as structural Verilog: 5 circuits, main circuit alu
module alu (
  input  [31:0] A,
  input  [31:0] B,
  input  [3:0] ALUSel,
  output [31:0] Result
);

  wire comparator_1_lt;
  wire [31:0] add0, and1, or2, sll6, slt7, sra5, srl4, xor3;

  Adder #(.width(32)) adder_1 (.a(A), .b(B), .out(add0));  // open: cin, cout
  assign and1 = A & B;  // AND_Gate and_1, 32 bits wide
  assign or2 = A | B;  // OR_Gate or_1, 32 bits wide
  assign xor3 = A ^ B;  // XOR_Gate xor_1, 32 bits wide
  Comparator #(.width(32)) comparator_1 (.a(A), .b(B), .lt(comparator_1_lt));  // open: gt, eq
  Multiplier #(.mode("twosComplement"), .width(32)) multiplier_1 ();  // open: a, b, out, cin, cout
  assign slt7 = {{31{1'b0}}, comparator_1_lt};  // Bit_Extender bit_extender_1
  srl32 srl32_1 (.in_1(A), .in_2(B), .out_3(srl4));
  sra32 sra32_1 (.in_1(A), .in_2(B), .out_3(sra5));
  sll32 sll32_1 (.in_1(A), .in_2(B), .out_3(sll6));

  // Notes on the sheet:
  //   INPUTS to your circuit
  //   DON'T CHANGE THE LOCATIONS OF THE INPUTS AND OUTPUTS!
  //   OUTPUT from your circuit
endmodule

module srl32 (
  input  [31:0] in_1,
  input  [31:0] in_2,
  output [31:0] out_3
);

  wire [4:0] bit_extender_1_out;

  Bit_Extender #(.in_width(32), .out_width(5), .\type ("zero")) bit_extender_1 (.in(in_2), .out(bit_extender_1_out));
  Shifter #(.shift("lr"), .width(32)) shifter_1 (.in(in_1), .\dist (bit_extender_1_out), .out(out_3));
endmodule

module sra32 (
  input  [31:0] in_1,
  input  [31:0] in_2,
  output [31:0] out_3
);

  wire [4:0] bit_extender_1_out;

  Bit_Extender #(.in_width(32), .out_width(5), .\type ("zero")) bit_extender_1 (.in(in_2), .out(bit_extender_1_out));
  Shifter #(.shift("ar"), .width(32)) shifter_1 (.in(in_1), .\dist (bit_extender_1_out), .out(out_3));
endmodule

module sll32 (
  input  [31:0] in_1,
  input  [31:0] in_2,
  output [31:0] out_3
);

  wire [4:0] bit_extender_1_out;

  Bit_Extender #(.in_width(32), .out_width(5), .\type ("zero")) bit_extender_1 (.in(in_2), .out(bit_extender_1_out));
  Shifter #(.width(32)) shifter_1 (.in(in_1), .\dist (bit_extender_1_out), .out(out_3));
endmodule

module mul32 (
  input  [3:0] mutiplicand,
  input  [3:0] multiplier
);

  wire bit_extender_2_out, clock_1_out, undriven, undriven_2;
  wire [3:0] register_1_q, shifter_2_out;
  wire [7:0] adder_1_out, bit_extender_1_out, multiplexer_1_out, multiplicand_q, product_q;

  assign bit_extender_1_out = {{4{1'b0}}, mutiplicand};  // Bit_Extender bit_extender_1
  Clock clock_1 (.out(clock_1_out));
  Register multiplicand (.D(bit_extender_1_out), .clk(undriven), .Q(multiplicand_q));  // open: en, clr
  Register #(.width(4)) register_1 (.D(multiplier), .clk(clock_1_out), .Q(register_1_q));  // open: en, clr
  Shifter shifter_1 (.in(multiplicand_q), .\dist (3'b001), .out(bit_extender_1_out));
  Shifter #(.shift("lr"), .width(4)) shifter_2 (.in(register_1_q), .\dist (2'b01), .out(shifter_2_out));
  Adder adder_1 (.a(multiplicand_q), .b(product_q), .out(adder_1_out));  // open: cin, cout
  Bit_Extender #(.in_width(4), .out_width(1), .\type ("zero")) bit_extender_2 (
    .in(shifter_2_out), .out(bit_extender_2_out));
  Multiplexer #(.enable("false"), .width(8)) multiplexer_1 (
    .in0({8{1'b0}}), .in1(adder_1_out), .out(multiplexer_1_out), .sel(bit_extender_2_out));
  Register product (.D(multiplexer_1_out), .clk(undriven_2), .Q(product_q));  // open: en, clr
endmodule
